# Fritzing sketch Self Sustaining Nightlight (saved by Fritzing 0.9.2b)
breadboards: 1

parts:
  Part1 = Arduino Mega ADK (Rev3)
  R1 = PHOTOCELL [package=photocell-kit]
  R2 = Resistor [tolerance=±5% resistance=220 package=THT]
  R3 = Resistor [tolerance=±5% resistance=220 package=THT]
  LED1 = LED - 5mm [color="Red (633nm)" package="5 mm [THT]"]

nets:
  N1: Part1.A0, R1.P$1, R2.Pin_1
  N2: Part1.GND, R2.Pin_0, R3.Pin_0
  N3: Part1.D10_PWM, LED1.anode
  N4: Part1.5V, R1.P$2
  N5: R3.Pin_1, LED1.cathode

// code stored in the sketch: NightLight.ino
// Pins
int sensorPin = A0;
int lightPin = 9;

// Variables
int lightState = 0;
int lowThreshold = 400;
int highTreshold = 600;
float startTime = 0;
float currentTime = 0;
boolean flag = false;
boolean night = false;  // if false it is a day, and if true it is a night
void setup() {
  
  // Start Serial & set pin to output	
  Serial.begin(9600);
  delay(100);
  pinMode(lightPin,OUTPUT);
  
}

void loop() {

  // Read the sensor pin
  int sensorValue = analogRead(sensorPin);
  Serial.println(sensorValue);
  //Serial.println()
  int interval = 3000;
  unsigned long time;
  
  
    if (sensorValue < lowThreshold){
      night = true;
    }else{
      night = false ;
      startTime = 0;
      flag = false;
    }
  if( !night ){
    
    digitalWrite(lightPin,LOW);
  }else if( night ){
    if( !flag ) {
    startTime = millis();
    flag = true;
    }
    currentTime = millis();
    
    if( currentTime - startTime < 6000 ){
      digitalWrite(lightPin,HIGH);
    }else{
      digitalWrite(lightPin,LOW);
    }
    
  
  }
  // If light level is low is detected, switch light on

  
/*  // If light level goes up again, switch the lights off
  if (sensorValue > highTreshold){ 
    digitalWrite(lightPin, LOW);
  } */
}


//
