# Fritzing sketch Smoke_Alarm (saved by Fritzing 0.9.2b)
breadboards: 1

parts:
  MQ2 = GAS_SENSOR [package=mq-3]
  Part1 = Arduino Uno (Rev3) - ICSP
  R1 = Resistor [tolerance=±5% resistance=220 package="1206 [SMD]"]
  LED1 = LED - 5mm [color="Green (565nm)" package="5 mm [THT]"]
  R2 = Resistor [tolerance=±5% resistance=220 package="1206 [SMD]"]
  LED2 = LED - 5mm [color="Yellow (595nm)" package="5 mm [THT]"]
  J1 = Piezo Speaker
  R3 = Resistor [tolerance=±5% resistance=220 package="1206 [SMD]"]
  LED3 = LED - 5mm [color="Red (633nm)" package="5 mm [THT]"]

nets:
  N1: MQ2.B1, MQ2.A1
  N2: MQ2.H1, Part1.A0
  N3: MQ2.H2, Part1.GND, R1.Pin_0, R2.Pin_0, J1.pin1, R3.Pin_0
  N4: Part1.ICSP_MOSI, Part1.D11_PWM/MOSI, LED1.anode
  N5: Part1.D9_PWM, LED3.anode
  N6: Part1.D10_PWM/SS, LED2.anode
  N7: Part1.D6_PWM, J1.pin2
  N8: R1.Pin_1, LED1.cathode
  N9: R2.Pin_1, LED2.cathode
  N10: R3.Pin_1, LED3.cathode

// code stored in the sketch: Smoke_Alarm.ino
const int gasPin = A0;                                             // gas pin Arduino analog A0
int smoke_level;

int led_G = 11;                                                    // the pin that the LED is attached to
int led_W = 10;
int led_D = 9;

int speakerOUT = 6;


                                                                  // the setup routine runs once when you press reset:
void setup() {
  Serial.begin(9600);                                             // Initalize serial port - 9600 bps
  
  pinMode(gasPin, INPUT);
  
  pinMode(led_G, OUTPUT);
  pinMode(led_W, OUTPUT);
  pinMode(led_D, OUTPUT);
  pinMode(speakerOUT, OUTPUT);
}

void loop() {
  
  smoke_level= analogRead(gasPin);                                 //arduino reads the value from the smoke sensor
  Serial.println(smoke_level);                                    //prints just for debugging purposes, to see what values the sensor is picking up

  if(smoke_level > 42){                                            //Warning state - Light loop & Sound Ping
     for(int fadeValue = 0 ; fadeValue <= 255; fadeValue +=5) { 
    analogWrite(led_W, fadeValue);         
    delay(30);                            
    } 

  // fade out from max to min in increments of 5 points:
    for(int fadeValue = 255 ; fadeValue >= 0; fadeValue -=5) { 
    analogWrite(led_W, fadeValue);         
    delay(30);                            
    } 

    tone(6, 523, 300);
    delay(300);

    digitalWrite(led_D,LOW);
    digitalWrite(led_G,LOW);      
    } 
  
  
    if(smoke_level > 80){                                            //Danger state - Light loop & Sound Ping
     for(int fadeValue = 0 ; fadeValue <= 255; fadeValue +=5) { 
      analogWrite(led_D, fadeValue);         
      delay(10);                            
    } 

  // fade out from max to min in increments of 5 points:
    for(int fadeValue = 255 ; fadeValue >= 0; fadeValue -=5) { 
      analogWrite(led_D, fadeValue);         
      delay(10);                            
    } 

    tone(6, 523, 300);
    delay(100);

    digitalWrite(led_W,LOW);
    digitalWrite(led_G,LOW);      
    } 
    
    
  else{                                        //All Clear State
    digitalWrite(led_G,HIGH);
    tone(6, 523, 300);
    delay(3000); 
    
    digitalWrite(led_W,LOW);
    digitalWrite(led_D,LOW);  
  }
  
}





// Goal create a wanring alarm for smoke
